# Fritzing sketch Talaria MX5 Killswitch (saved by Fritzing 0.8.7b)

parts:
  D2 = Rectifier Diode [part_number=1N4007 package="300 mil [THT]"]
  U3 = TEMPERATURE-SENSOR [package=to-92]
  U1 = SWITCH_SPDT [package=kps-1290]
  JP1 = Header 3 [package=molex-1x3_lock]
  JP2 = Header 3 [package=molex-1x3_lock]
  JP3 = Header 3 [package=molex-1x3_lock]
  JP4 = Header 3 [package=molex-1x3_lock]
  F1 = FUSE [package=fuse_5mm]
  U2 = RELAY [package=relay-g5q]
  Controller = Arduino Nano (Rev3.0)

nets:
  N1: D2.cathode, U1.P, U1.S, U2.COIL2
  N2: D2.anode, JP2.2, JP4.2, U2.NO, U2.COIL1
  N3: U3.GND, JP3.3
  N4: U3.ADJ, JP3.2
  N5: U3.VCC, JP3.1
  N6: U1.O, JP4.1, F1.2
  N7: JP1.1, Controller.VIN
  N8: JP1.2, Controller.GND
  N9: JP1.3, Controller.A7
  N10: JP2.1, U2.MAIN
  N11: JP2.3, F1.1
  N12: JP4.3, U2.NC
